// Logisim project récupe Madoc.circ as structural Verilog
module _1bit_adder (
  input  A,
  input  B,
  input  Cin,
  output S,
  output G,
  output P
);

  wire xor_1_out;

  and and_1 (G, A, B);
  or or_1 (P, A, B);
  xor xor_1 (xor_1_out, A, B);
  xor xor_2 (S, xor_1_out, Cin);
endmodule

module _4bit_adder (
  input  [3:0] A,
  input  [3:0] B,
  input  Cin,
  output [3:0] S,
  output Cout
);

  wire n1bit_adder_1_g, n1bit_adder_1_p, n1bit_adder_2_g, n1bit_adder_2_p, n1bit_adder_3_g, n1bit_adder_3_p,
       n1bit_adder_4_g, n1bit_adder_4_p, n4bit_carrylookahaed_1_c1, n4bit_carrylookahaed_1_c2,
       n4bit_carrylookahaed_1_c3;

  _1bit_adder u_1bit_adder_1 (.A(A[0]), .B(B[0]), .S(S[0]), .G(n1bit_adder_1_g), .P(n1bit_adder_1_p), .Cin(Cin));
  _1bit_adder u_1bit_adder_2 (
    .A(A[1]), .B(B[1]), .S(S[1]), .G(n1bit_adder_2_g), .P(n1bit_adder_2_p), .Cin(n4bit_carrylookahaed_1_c1));
  _1bit_adder u_1bit_adder_3 (
    .A(A[2]), .B(B[2]), .S(S[2]), .G(n1bit_adder_3_g), .P(n1bit_adder_3_p), .Cin(n4bit_carrylookahaed_1_c2));
  _1bit_adder u_1bit_adder_4 (
    .A(A[3]), .B(B[3]), .S(S[3]), .G(n1bit_adder_4_g), .P(n1bit_adder_4_p), .Cin(n4bit_carrylookahaed_1_c3));
  _4bit_carrylookahaed u_4bit_carrylookahaed_1 (
    .C0(Cin), .P0(n1bit_adder_1_p), .G0(n1bit_adder_1_g), .P1(n1bit_adder_2_p), .G1(n1bit_adder_2_g),
    .P2(n1bit_adder_3_p), .G2(n1bit_adder_3_g), .P3(n1bit_adder_4_p), .G3(n1bit_adder_4_g),
    .C1(n4bit_carrylookahaed_1_c1), .C2(n4bit_carrylookahaed_1_c2), .C3(n4bit_carrylookahaed_1_c3), .C4(Cout));
endmodule

module _4bit_carrylookahaed (
  input  C0,
  input  P0,
  input  G0,
  input  P1,
  input  G1,
  input  P2,
  input  G2,
  input  P3,
  input  G3,
  output C1,
  output C2,
  output C3,
  output C4
);

  wire and_1_out, and_2_out, and_3_out, and_4_out, and_5_out, and_6_out, and_7_out, and_8_out, and_9_out,
       and_10_out;

  and and_1 (and_1_out, C0, P0);
  or or_1 (C1, and_1_out, G0);
  and and_2 (and_2_out, C0, P0, P1);
  and and_3 (and_3_out, G0, P1);
  or or_2 (C2, and_2_out, and_3_out, G1);
  and and_4 (and_4_out, C0, P0, P1, P2);
  and and_5 (and_5_out, G0, P1, P2);
  and and_6 (and_6_out, G1, P2);
  and and_7 (and_7_out, C0, P0, P1, P2, P3);
  and and_8 (and_8_out, G0, P1, P2, P3);
  and and_9 (and_9_out, G1, P2, P3);
  and and_10 (and_10_out, G2, P3);
  or or_3 (C3, and_4_out, and_5_out, and_6_out, G2);
  or or_4 (C4, and_7_out, and_8_out, and_9_out, and_10_out, G3);
endmodule
